# Fritzing sketch pcb (saved by Fritzing 0.9.3b)
circuit board: 8.46667cm x 5.64444cm
circuit board: 21cm x 14cm
breadboards: 1

parts:
  Componente1 = Arduino Nano (Rev3.0) (ICSP)
  R1 = Resistor [tolerance=±5% resistance=2.2k package=THT]
  Q4 = npn-Powertransistor [package="TO220 [THT]"]
  J9 = female pin header, 2 pins [form="♀ (female)"]
  J10 = female pin header, 2 pins [form="♀ (female)"]
  L1 = Solenoid  # not connected
  D1 = Diode [package=diode-hv]

nets:
  N1: Componente1.D2, R1.Pin_0
  N2: Componente1.VIN, J9.pin1, J10.pin1, D1.A
  N3: Componente1.GND, Q4.emitter, J9.pin2
  N4: R1.Pin_1, Q4.base
  N5: Q4.collector, J10.pin2, D1.C

notes:
  2.2KΩ
  1N4007
  TIP120
  12V
  -
  +
  ELECTROVALVE
  ARDUINO NANO V3
  VALVE
