# Fritzing sketch project (saved by Fritzing 0.9.3b)
circuit board: 4.28829cm x 5.61332cm
breadboards: 1

parts:
  Componente1 = Arduino Nano (Rev3.0) (ICSP)
  R1 = Resistor [tolerance=±5% resistance=2.2k package=THT]
  Q4 = npn-Powertransistor [package="TO220 [THT]"]
  J9 = female pin header, 2 pins [form="♀ (female)"]
  J10 = female pin header, 2 pins [form="♀ (female)"]
  L1 = Solenoid  # not connected
  D1 = Diode [package=diode-hv]
  U1 = LCD-16X2 [package=lcd-16x2_noholes]  # not connected
  J17 = female pin header, 4 pins [form="♀ (female)"]
  S3 = Round Pushbutton  # not connected
  S4 = Round Pushbutton  # not connected
  J38 = female pin header, 2 pins [form="♀ (female)"]
  J39 = female pin header, 2 pins [form="♀ (female)"]
  R2 = Resistor [tolerance=±5% resistance=2.2k package=THT]
  R3 = Resistor [tolerance=±5% resistance=2.2k package=THT]
  S5 = Round Pushbutton  # not connected
  J40 = female pin header, 2 pins [form="♀ (female)"]
  R4 = Resistor [tolerance=±5% resistance=2.2k package=THT]

nets (from the pcb view):
  N1: Componente1.D2, R1.Pin_0
  N2: Componente1.VIN, J9.pin1, J10.pin1, D1.C
  N3: Componente1.GND, Q4.emitter, J9.pin2, J17.pin1, R2.Pin_0, R3.Pin_0, R4.Pin_0
  N4: Componente1.5V, J17.pin2, J38.pin1, J39.pin1, J40.pin1
  N5: Componente1.A5, J17.pin4
  N6: Componente1.A4, J17.pin3
  N7: Componente1.A3, J39.pin2, R3.Pin_1
  N8: Componente1.A2, J38.pin2, R2.Pin_1
  N9: Componente1.A1, J40.pin2, R4.Pin_1
  N10: R1.Pin_1, Q4.base
  N11: Q4.collector, J10.pin2, D1.A

notes:
  2.2KΩ
  1N4007
  TIP120
  12V
  -
  +
  ELECTROVALVE
  ARDUINO NANO V3
  VALVE
  LCD with I2C interface
  LCD
  GND
  VCC
  SDA
  SCL
  5V
  10KΩ
